// Logisim project D-ff.circ as structural Verilog: 1 circuit, main circuit main
module main (
  input  in_1,
  input  in_2,
  output out_3,
  output out_4,
  output out_5
);

  wire d_ff_1_qn, d_ff_2_qn, d_ff_3_qn, not_1_out;

  not not_1 (not_1_out, in_1);
  D_Flip_Flop d_ff_1 (.clk(not_1_out), .D(d_ff_1_qn), .Q(out_3), .Qn(d_ff_1_qn));  // open: preset, en, reset
  D_Flip_Flop d_ff_2 (.clk(d_ff_1_qn), .D(d_ff_2_qn), .Q(out_4), .Qn(d_ff_2_qn));  // open: preset, en, reset
  D_Flip_Flop d_ff_3 (.clk(d_ff_2_qn), .D(d_ff_3_qn), .Q(out_5), .Qn(d_ff_3_qn));  // open: preset, en, reset
endmodule
